# Fritzing sketch Faduino (saved by Fritzing 0.9.3b)
breadboards: 1

parts:
  IC1 = L293D [package=THT]
  U1 = SLIDER [package=slider]
  M1 = DC Motor
  R1 = Resistor [tolerance=±5% resistance=1M package="2010 [SMD]"]
  VCC1 = Battery block 9V
  C1 = Electrolytic Capacitor [capacitance=10µF package="100 mil [THT, electrolytic]"]
  Pro_Micro3 = Pro Micro

nets:
  N1: IC1.In_1, Pro_Micro3.D7
  N2: IC1.Out_1_(_Controlled_by_Enable_1_), M1.pin_1
  N3: IC1.0V, U1.E, VCC1.-, C1.-
  N4: IC1.Out_2_(_Controlled_by_Enable_1_), M1.pin_2
  N5: IC1.In_2, Pro_Micro3.D8
  N6: IC1.+Vmotor, VCC1.+
  N7: IC1.+V, U1.A, C1.+
  N8: U1.S, Pro_Micro3.D18/A0
  N9: R1.Pin_0, Pro_Micro3.D10
  N10: R1.Pin_1, Pro_Micro3.D16/MOSI

notes:
  Fade Touch Line
  1M ohm
  10uF
  by Gustavo Silveira
  musiconerd.com

custom parts:
  Pro Micro: The SparkFun Pro Micro is a complete USB-based microcontoller development system, in a very small footprint, capable of implementing many types of projects. All programming can be done via the USB port.
